// Logisim project labo4.circ as structural Verilog: 3 circuits, main circuit SHREGI_4BITS
module SHREGI_4BITS (
  input  [3:0] D,
  input  R,
  input  L,
  input  [1:0] S,
  input  CLR,
  input  CLK,
  output [3:0] Q
);

  wire multiplexer_1_out, multiplexer_2_out, multiplexer_3_out, multiplexer_4_out;

  Multiplexer #(.select(2), .enable("false")) multiplexer_1 (
    .in0(Q[3]), .in1(Q[2]), .in2(D[3]), .in3(R), .out(multiplexer_1_out), .sel(S));
  D_Flip_Flop d_ff_1 (.D(multiplexer_1_out), .clk(CLK), .Q(Q[3]), .reset(CLR));  // open: Qn, preset
  Multiplexer #(.select(2), .enable("false")) multiplexer_2 (
    .in0(Q[2]), .in1(Q[1]), .in2(D[2]), .in3(Q[3]), .out(multiplexer_2_out), .sel(S));
  D_Flip_Flop d_ff_2 (.D(multiplexer_2_out), .clk(CLK), .Q(Q[2]), .reset(CLR));  // open: Qn, preset
  Multiplexer #(.select(2), .enable("false")) multiplexer_3 (
    .in0(Q[1]), .in1(Q[0]), .in2(D[1]), .in3(Q[2]), .out(multiplexer_3_out), .sel(S));
  D_Flip_Flop d_ff_3 (.D(multiplexer_3_out), .clk(CLK), .Q(Q[1]), .reset(CLR));  // open: Qn, preset
  Multiplexer #(.select(2), .enable("false")) multiplexer_4 (
    .in0(Q[0]), .in1(L), .in2(D[0]), .in3(Q[1]), .out(multiplexer_4_out), .sel(S));
  D_Flip_Flop d_ff_4 (.D(multiplexer_4_out), .clk(CLK), .Q(Q[0]), .reset(CLR));  // open: Qn, preset

  // Notes on the sheet:
  //   Attention, votre version de Logisim
  //   ne contient pas de tracker. Si vous
  //   enregistrez votre projet, toutes les
  //   informations du tracker seront
  //   définitivement effacées.
endmodule

module SHREGI_8BITS (
  input  in_1,
  input  in_2,
  input  [1:0] in_3,
  input  [7:0] in_4,
  input  in_5,
  output [7:0] out_6
);

  wire clock_1_out;

  Clock clock_1 (.out(clock_1_out));
  SHREGI_4BITS shregi_4bits_1 (
    .D(in_4[3:0]), .R(in_1), .L(in_2), .S(in_3), .CLR(in_5), .CLK(clock_1_out), .Q(out_6[3:0]));
  SHREGI_4BITS shregi_4bits_2 (
    .D(in_4[7:4]), .R(in_1), .L(in_2), .S(in_3), .CLR(in_5), .CLK(clock_1_out), .Q(out_6[7:4]));

  // Notes on the sheet:
  //   Attention, votre version de Logisim
  //   ne contient pas de tracker. Si vous
  //   enregistrez votre projet, toutes les
  //   informations du tracker seront
  //   définitivement effacées.
endmodule

module LFSR_8BITS (
);

  wire CLK_out, xnor_1_out, xnor_2_out, xnor_3_out;
  wire [3:0] Q0, Q1;

  Hex_Digit_Display hex_digit_display_1 (.value(Q0));  // open: dp
  Clock CLK (.out(CLK_out));
  Hex_Digit_Display hex_digit_display_2 (.value(Q1));  // open: dp
  D_Flip_Flop d_ff_1 (.D(xnor_1_out), .clk(CLK_out), .Q(Q0[0]));  // open: Qn, preset, reset
  D_Flip_Flop d_ff_2 (.D(Q0[0]), .clk(CLK_out), .Q(Q0[1]));  // open: Qn, preset, reset
  xnor xnor_1 (xnor_1_out, xnor_2_out, Q0[3]);
  D_Flip_Flop d_ff_3 (.D(Q0[1]), .clk(CLK_out), .Q(Q0[2]));  // open: Qn, preset, reset
  xnor xnor_2 (xnor_2_out, xnor_3_out, Q1[0]);
  xnor xnor_3 (xnor_3_out, Q1[3], Q1[1]);
  D_Flip_Flop d_ff_4 (.D(Q0[2]), .clk(CLK_out), .Q(Q0[3]));  // open: Qn, preset, reset
  D_Flip_Flop d_ff_5 (.D(Q0[3]), .clk(CLK_out), .Q(Q1[0]));  // open: Qn, preset, reset
  D_Flip_Flop d_ff_6 (.D(Q1[0]), .clk(CLK_out), .Q(Q1[1]));  // open: Qn, preset, reset
  D_Flip_Flop d_ff_7 (.D(Q1[1]), .clk(CLK_out), .Q(Q1[2]));  // open: Qn, preset, reset
  D_Flip_Flop d_ff_8 (.D(Q1[2]), .clk(CLK_out), .Q(Q1[3]));  // open: Qn, preset, reset

  // Notes on the sheet:
  //   Attention, votre version de Logisim
  //   ne contient pas de tracker. Si vous
  //   enregistrez votre projet, toutes les
  //   informations du tracker seront
  //   définitivement effacées.
endmodule
